# Fritzing sketch pendulo (saved by Fritzing 0.9.3b)

parts:
  Raspberry_Pi_2 = Raspberry Pi 3 [part_number=RPI-3-V1.2]
  U1 = TCRT5000 Line Tracker

nets:
  N1: Raspberry_Pi_2.GND, U1.Do

custom parts:
  TCRT5000 Line Tracker: A line tracker module based on TCRT5000 (Vishay)
